# Fritzing sketch Simple Arduino Battery Analyzer - Charger with Sense on battery (saved by Fritzing 0.9.4)
breadboards: 1

parts:
  R3 = Resistor [tolerance=±5% resistance=0.15 power=5W package=THT]
  Arduino_Uno1 = Arduino Uno (Rev3) - ICSP
  BAT2 = Battery Holders [package=battery-aa]
  Q2 = Basic FET N-Channel [part_number=IRLZ44N package="TO220 [THT]"]
  R4 = Resistor [tolerance=±5% resistance=4.7k package="1206 [SMD]"]
  C2 = Capacitor [part_number=1uF package=cap-pth-5mm]
  R5 = Resistor [tolerance=±5% resistance=4.7k package="1206 [SMD]"]
  R6 = Resistor [tolerance=±5% resistance=4.7k package="1206 [SMD]"]
  R7 = Resistor [tolerance=±5% resistance=4.7k package="1206 [SMD]"]
  C3 = Capacitor [part_number=1uF package=cap-pth-5mm]
  Power_plug1 = Power plug
  Q5 = Basic FET P-Channel [part_number=IRF4905 package="TO220 [THT]"]
  M1 = DC Motor [part_number=fan]

nets:
  N1: R3.Pin_0, Q2.drain, R6.Pin_1, Q5.drain
  N2: R3.Pin_1, BAT2.+, R5.Pin_1
  N3: Arduino_Uno1.A0, R6.Pin_0
  N4: Arduino_Uno1.A1, R5.Pin_0
  N5: Arduino_Uno1.D9_PWM, R7.Pin_0
  N6: Arduino_Uno1.D10_PWM/SS, R4.Pin_0
  GND: Arduino_Uno1.GND, BAT2.-, Q2.source, C2.2, C3.2, Power_plug1.GND, M1.pin_2
  N7: Q2.gate, R4.Pin_1, C2.1
  N8: R7.Pin_1, C3.1, Q5.gate
  5V: Power_plug1.VCC, Q5.source, M1.pin_1
