# Fritzing sketch Simple Arduino Battery Analyzer - UI (saved by Fritzing 0.9.4)
breadboards: 3

parts:
  Part1 = Arduino Uno (Rev3) - ICSP
  U1 = mystery part, 5 pins [chip_label=?]
  M2 = DC Motor [part_number=fan]
  Q6 = Basic FET P-Channel [part_number=IRF4905 package="TO220 [THT]"]
  Power_plug2 = Power plug
  R8 = Resistor [tolerance=±5% resistance=0.15 power=5W package=THT]
  BAT3 = Battery Holders [package=battery-aa]
  Q7 = Basic FET N-Channel [part_number=IRLZ44N package="TO220 [THT]"]
  C4 = Capacitor [part_number=1uF package=cap-pth-5mm]
  C5 = Capacitor [part_number=1uF package=cap-pth-5mm]
  R9 = Resistor [tolerance=±5% resistance=4.7k package="1206 [SMD]"]
  R10 = Resistor [tolerance=±5% resistance=4.7k package="1206 [SMD]"]
  R11 = Resistor [tolerance=±5% resistance=4.7k package="1206 [SMD]"]
  R12 = Resistor [tolerance=±5% resistance=4.7k package="1206 [SMD]"]
  Arduino_Robot_LCD = mystery part, 10 pins [chip_label=?]

nets (from the schematic view):
  N1: Part1.A2, U1.pin3
  N2: Part1.A3, U1.pin4
  N3: Part1.A4/SDA, R9.Pin_0
  N4: Part1.A5/SCL, R10.Pin_0
  5V: Part1.5V, U1.pin2, M2.pin_1, Q6.source, Power_plug2.VCC, Arduino_Robot_LCD.pin2, Arduino_Robot_LCD.pin10
  N5: Part1.D8, Arduino_Robot_LCD.pin3
  N6: Part1.D9_PWM, R12.Pin_0
  N7: Part1.D10_PWM/SS, R11.Pin_0
  N8: Part1.D11_PWM/MOSI, Arduino_Robot_LCD.pin7
  N9: Part1.D12/MISO, Arduino_Robot_LCD.pin9
  N10: Part1.D13/SCK, Arduino_Robot_LCD.pin8
  GND: Part1.GND, U1.pin1, M2.pin_2, Power_plug2.GND, BAT3.-, Q7.source, C4.2, C5.2, Arduino_Robot_LCD.pin1
  N11: Part1.D0/RX, U1.pin5
  N12: Part1.D4, Arduino_Robot_LCD.pin5
  N13: Part1.D6_PWM, Arduino_Robot_LCD.pin4
  N14: Part1.D7, Arduino_Robot_LCD.pin6
  N15: Q6.gate, C4.1, R11.Pin_1
  N16: Q6.drain, R8.Pin_0, Q7.drain, R9.Pin_1
  N17: R8.Pin_1, BAT3.+, R10.Pin_1
  N18: Q7.gate, C5.1, R12.Pin_1
