# Fritzing sketch Simple Arduino Battery Analyzer (saved by Fritzing 0.9.4)
breadboards: 1

parts:
  R3 = Resistor [tolerance=±5% resistance=0.15 power=5W package=THT]
  Arduino_Uno1 = Arduino Uno (Rev3) - ICSP
  BAT2 = Battery Holders [package=battery-aa]
  Q2 = Basic FET N-Channel [part_number=IRLZ44N package="TO220 [THT]"]
  R4 = Resistor [tolerance=±5% resistance=4.7k package="1206 [SMD]"]
  C2 = Capacitor [part_number=1uF package=cap-pth-5mm]
  R5 = Resistor [tolerance=±5% resistance=4.7k package="1206 [SMD]"]
  R6 = Resistor [tolerance=±5% resistance=4.7k package="1206 [SMD]"]

nets:
  GND: R3.Pin_0, Arduino_Uno1.GND, BAT2.-, C2.2
  N1: R3.Pin_1, Q2.source, R6.Pin_1
  N2: Arduino_Uno1.A0, R6.Pin_0
  N3: Arduino_Uno1.A1, R5.Pin_0
  N4: Arduino_Uno1.D9_PWM, R4.Pin_0
  N5: BAT2.+, Q2.drain, R5.Pin_1
  N6: Q2.gate, R4.Pin_1, C2.1
