# Fritzing sketch Simple Arduino Battery Charger (saved by Fritzing 0.9.4)
breadboards: 1

parts:
  Q1 = Basic FET N-Channel [part_number=IRLZ44N package="TO220 [THT]"]
  R1 = Resistor [tolerance=±5% resistance=4.7k package="1206 [SMD]"]
  Part1 = Arduino Uno (Rev3)
  C1 = Capacitor [part_number=1uF package=cap-pth-small]
  R2 = Resistor [tolerance=±5% resistance=220 package="1206 [SMD]"]
  U1 = LM 358 Dual Op-Amp [package="DIP8 [THT]"]
  DC9V = Power plug
  R3 = Resistor [tolerance=±5% resistance=4.7k package="1206 [SMD]"]
  VCC1 = Battery
  Rsense = Resistor [tolerance=±5% resistance=0.15 package=THT]
  DC5V = Power plug

nets:
  N1: Q1.gate, U1.connector6
  5V: Q1.drain, DC5V.VCC
  N2: Q1.source, Part1.A5/SCL, R2.Pin_1, R3.Pin_0, VCC1.+
  N3: R1.Pin_0, Part1.D9_PWM
  N4: R1.Pin_1, C1.1, U1.connector4
  N5: Part1.A4/SDA, VCC1.-, Rsense.Pin_1
  GND: Part1.GND, C1.2, U1.connector3, DC9V.GND, R3.Pin_1, Rsense.Pin_0, DC5V.GND
  N6: R2.Pin_0, U1.connector5
  9V: U1.connector7, DC9V.VCC
