# Fritzing sketch Simple Arduino Battery Discharger 2 (saved by Fritzing 0.9.4)
breadboards: 1

parts:
  Arduino_Uno = Arduino Uno (Rev3) - ICSP
  BAT1 = Battery Holders [package=battery-aa]
  Q1 = Basic FET N-Channel [part_number=IRFZ44N package="TO220 [THT]"]
  R1 = Resistor [tolerance=±5% resistance=1 power=5W package=THT]
  DS1 = DS18B20 1-Wire Temperature Sensor [part_number=DS18B20]
  R2 = Resistor [tolerance=±5% resistance=4.7k package=THT]

nets:
  N1: Arduino_Uno.A4/SDA, Q1.drain, R1.Pin_0
  N2: Arduino_Uno.A5/SCL, BAT1.+, R1.Pin_1
  5V: Arduino_Uno.5V, DS1.VDD, R2.Pin_0
  GND: Arduino_Uno.GND, BAT1.-, Q1.source, DS1.GND
  N3: Arduino_Uno.D2, Q1.gate
  N4: Arduino_Uno.D3_PWM, DS1.DQ, R2.Pin_1
