# Fritzing sketch Simple Arduino Battery Discharger 3 (saved by Fritzing 0.9.4)
breadboards: 1

parts:
  R3 = Resistor [tolerance=±5% resistance=1 power=5W package=THT]
  Arduino_Uno1 = Arduino Uno (Rev3) - ICSP
  BAT2 = Battery Holders [package=battery-aa]
  Q2 = Basic FET N-Channel [part_number=IRFZ44N package="TO220 [THT]"]
  DS2 = DS18B20 1-Wire Temperature Sensor [part_number=DS18B20]
  R4 = Resistor [tolerance=±5% resistance=4.7k package=THT]

nets:
  N1: R3.Pin_0, Arduino_Uno1.A4/SDA, Q2.drain
  N2: R3.Pin_1, Arduino_Uno1.A5/SCL, BAT2.+
  5V: Arduino_Uno1.5V, DS2.VDD, R4.Pin_0
  GND: Arduino_Uno1.GND, BAT2.-, Q2.source, DS2.GND
  N3: Arduino_Uno1.D2, Q2.gate
  N4: Arduino_Uno1.D3_PWM, DS2.DQ, R4.Pin_1
