# Fritzing sketch Simple Arduino Battery Discharger 4 (saved by Fritzing 0.9.4)
breadboards: 1

parts:
  R3 = Resistor [tolerance=±5% resistance=1 power=5W package=THT]
  Arduino_Uno1 = Arduino Uno (Rev3) - ICSP
  BAT2 = Battery Holders [package=battery-aa]
  Q2 = Basic FET N-Channel [part_number=IRLZ44N package="TO220 [THT]"]
  C1 = Ceramic Capacitor [capacitance=10nF package="100 mil [THT, multilayer]"]
  U1 = LM 358 Dual Op-Amp [package="DIP8 [THT]"]
  R5 = Resistor [tolerance=±5% resistance=15k package=THT]

nets (from the schematic view):
  GND: R3.Pin_0, Arduino_Uno1.GND, BAT2.-, C1.0, U1.connector3
  N1: R3.Pin_1, Arduino_Uno1.A4/SDA, Q2.source, U1.connector1
  N2: Arduino_Uno1.A5/SCL, BAT2.+, Q2.drain
  N3: Arduino_Uno1.D2, R5.Pin_0
  N4: Arduino_Uno1.5V, U1.connector7
  N5: Q2.gate, U1.connector0
  N6: C1.1, U1.connector2, R5.Pin_1
