# Fritzing sketch Simple Arduino Battery Discharger (saved by Fritzing 0.9.4)
circuit board: 8.46667cm x 5.64444cm
breadboards: 1

parts:
  Part1 = Arduino Uno (Rev3)
  Q1 = Basic FET N-Channel [package="TO220 [THT]"]
  VCC1 = Battery
  R1 = Resistor [tolerance=±5% resistance=1 package=THT]

nets:
  N1: Part1.A4/SDA, Q1.drain, R1.Pin_0
  N2: Part1.A5/SCL, VCC1.+, R1.Pin_1
  N3: Part1.D2, Q1.gate
  N4: Part1.GND, Q1.source, VCC1.-
